// Logisim project Four_Bits_Add_Sub.circ as structural Verilog: 2 circuits, main circuit Add_Sub_4Bits
module Add_Sub_4Bits (
  input  [3:0] A,
  input  [3:0] B,
  input  Add_Sub,
  output [3:0] R,
  output Zero,
  output Overflow,
  output out_7,
  output out_8,
  output out_9,
  output out_10,
  output out_11,
  output out_12,
  output out_13,
  output out_14
);

  // Probe on A
  // Probe on B
  or or_1 (out_7, A[0], B[0]);
  and and_1 (out_8, A[0], B[0]);
  or or_2 (out_9, B[1], A[1]);
  and and_2 (out_10, B[1], A[1]);
  or or_3 (out_11, B[2], A[2]);
  and and_3 (out_12, B[2], A[2]);
  or or_4 (out_13, B[3], A[3]);
  and and_4 (out_14, B[3], A[3]);
  // Probe on R

  // Notes on the sheet:
  //   Simon Zheng 260744353
  //   MAKE SURE THAT YOU OPENED THIS PROJECT IN "LOGISIM-EVOLUTION"
  //   YOU CAN FIND "LOGISIM-EVOLUTION" PROGRAM IN THE ASSIGNMENT'S FOLDER
  //   DO NOT USE "LOGISIM" VERSION TO SOLVE THIS ASSIGNMENT!
endmodule

module Add_1Bit (
  input  Cin,
  input  A,
  input  B,
  output Sum,
  output Cout
);


  // Notes on the sheet:
  //   YOUR NAME AND STUDENT NUMBER HERE
  //   MAKE SURE THAT YOU OPENED THIS PROJECT IN "LOGISIM-EVOLUTION"
  //   YOU CAN FIND "LOGISIM-EVOLUTION" PROGRAM IN THE ASSIGNMENT'S FOLDER
  //   DO NOT USE "LOGISIM" VERSION TO SOLVE THIS ASSIGNMENT!
endmodule
